// Logisim project Physics111A_Final.circ as structural Verilog: 1 circuit, main circuit main
module main (
  input  in_1,
  input  in_2,
  input  in_3,
  input  in_4,
  input  in_5,
  input  in_6,
  input  in_7,
  input  in_8,
  input  in_9,
  input  in_10,
  input  in_11,
  input  in_12,
  input  in_13,
  input  in_14,
  input  in_15,
  input  in_16
);

  wire and_1_out, and_2_out, and_3_out, and_4_out, and_5_out, and_6_out, and_7_out, and_8_out, and_9_out,
       and_10_out, and_11_out, and_12_out, and_13_out, nand_1_out, nand_2_out, nand_3_out, nand_4_out,
       nand_5_out, nand_6_out, nand_7_out, nand_8_out, nand_9_out, nand_10_out, nand_11_out, nand_12_out,
       nand_13_out, nand_14_out, nand_15_out, nand_16_out, not_1_out, not_2_out, not_3_out, not_4_out;

  not not_1 (not_1_out, in_15);
  and and_1 (and_1_out, not_1_out, in_16);
  and and_2 (and_2_out, in_15, in_16);
  Demultiplexer #(.select(4)) demultiplexer_1 (
    .out0(in_1), .out1(in_1), .out2(in_1), .out3(in_1), .out4(in_1), .out5(in_1), .out6(in_1), .out7(in_1),
    .out8(in_1), .out9(in_1), .out10(in_1), .sel({in_15, in_14, in_13, in_12}));  // open: out11, out12, out13, out14, out15, in
  not not_2 (not_2_out, in_14);
  not not_3 (not_3_out, in_13);
  not not_4 (not_4_out, in_12);
  nand nand_1 (nand_1_out, not_4_out, not_3_out, not_2_out, and_1_out);
  nand nand_2 (nand_2_out, in_12, not_3_out, not_2_out, and_1_out);
  nand nand_3 (nand_3_out, not_4_out, in_13, not_2_out, and_1_out);
  nand nand_4 (nand_4_out, in_12, in_13, not_2_out, and_1_out);
  nand nand_5 (nand_5_out, not_4_out, not_3_out, in_14, and_1_out);
  nand nand_6 (nand_6_out, in_12, not_3_out, in_14, and_1_out);
  nand nand_7 (nand_7_out, not_4_out, in_13, in_14, and_1_out);
  nand nand_8 (nand_8_out, in_12, in_13, in_14, and_1_out);
  nand nand_9 (nand_9_out, not_4_out, not_3_out, not_2_out, and_2_out);
  nand nand_10 (nand_10_out, in_12, not_3_out, not_2_out, and_2_out);
  nand nand_11 (nand_11_out, not_4_out, in_13, not_2_out, and_2_out);
  nand nand_12 (nand_12_out, in_12, in_13, not_2_out, and_2_out);
  nand nand_13 (nand_13_out, not_4_out, not_3_out, in_14, and_2_out);
  nand nand_14 (nand_14_out, in_12, not_3_out, in_14, and_2_out);
  nand nand_15 (nand_15_out, not_4_out, in_13, in_14, and_2_out);
  nand nand_16 (nand_16_out, in_12, in_13, in_14, and_2_out);
  and and_3 (and_3_out, nand_11_out, nand_12_out);
  and and_4 (and_4_out, nand_10_out, and_3_out);
  and and_5 (and_5_out, nand_9_out, and_4_out);
  and and_6 (and_6_out, nand_8_out, and_5_out);
  and and_7 (and_7_out, nand_6_out, and_8_out);
  and and_8 (and_8_out, nand_7_out, and_6_out);
  and and_9 (and_9_out, nand_5_out, and_7_out);
  and and_10 (and_10_out, nand_4_out, and_9_out);
  and and_11 (and_11_out, nand_3_out, and_10_out);
  and and_12 (and_12_out, nand_2_out, and_11_out);
  // Probe on and_13_out
  and and_13 (and_13_out, nand_1_out, and_12_out);
  // Probe on and_12_out
  // Probe on and_11_out
  // Probe on and_10_out
  // Probe on and_9_out
  // Probe on and_7_out
  // Probe on and_8_out
  // Probe on and_6_out
  // Probe on and_5_out
  // Probe on and_4_out
  // Probe on and_3_out
  // Probe on nand_12_out
  // Probe on nand_13_out
  // Probe on nand_14_out
  // Probe on nand_15_out
  // Probe on nand_16_out

  assign in_2 = in_1;
  assign in_3 = in_1;
  assign in_4 = in_1;
  assign in_5 = in_1;
  assign in_6 = in_1;
  assign in_7 = in_1;
  assign in_8 = in_1;
  assign in_9 = in_1;
  assign in_10 = in_1;
  assign in_11 = in_1;

  // Other names for the same wires on the sheet: b0 = in_12; b1 = in_13; b2 = in_14; b3 = in_15; D = in_16

  // Notes on the sheet:
  //   ADC 1 Output
  //   ADC 2 Output
endmodule
